// Logisim project ALU.circ as structural Verilog: 2 circuits, main circuit 4-Bits Adder/Subtractor
module _4_Bits_Adder_Subtractor (
  input  in_1,
  input  [3:0] A,
  input  [3:0] B,
  output [3:0] A___B,
  output out_5
);

  wire _1_Bit_Adder_cout, full_adder_1_cout, full_adder_2_cout, xor_1_out, xor_2_out, xor_3_out, xor_4_out;

  xor xor_1 (xor_1_out, in_1, B[0]);
  xor xor_2 (xor_2_out, in_1, B[1]);
  xor xor_3 (xor_3_out, in_1, B[2]);
  xor xor_4 (xor_4_out, in_1, B[3]);
  Full_Adder _1_Bit_Adder (.A(A[0]), .B(xor_1_out), .Cin(in_1), .Sum(A___B[0]), .Cout(_1_Bit_Adder_cout));
  Full_Adder full_adder_1 (.A(A[1]), .B(xor_2_out), .Cin(_1_Bit_Adder_cout), .Sum(A___B[1]), .Cout(full_adder_1_cout));
  Full_Adder full_adder_2 (.A(A[2]), .B(xor_3_out), .Cin(full_adder_1_cout), .Sum(A___B[2]), .Cout(full_adder_2_cout));
  Full_Adder full_adder_3 (.A(A[3]), .B(xor_4_out), .Cin(full_adder_2_cout), .Sum(A___B[3]), .Cout(out_5));
endmodule

module Multiplier (
  input  [3:0] A,
  input  [3:0] B,
  output [7:0] A___B
);

  wire _1_Bit_Adder_cout, and_2_out, and_3_out, and_4_out, and_5_out, and_6_out, and_7_out, and_8_out,
       and_9_out, and_10_out, and_11_out, and_12_out, and_13_out, and_14_out, and_15_out, and_16_out,
       full_adder_1_cout, full_adder_1_sum, full_adder_2_cout, full_adder_2_sum, full_adder_3_cout,
       full_adder_3_sum, full_adder_4_cout, full_adder_5_cout, full_adder_5_sum, full_adder_6_cout,
       full_adder_6_sum, full_adder_7_cout, full_adder_7_sum, full_adder_8_cout, full_adder_9_cout,
       full_adder_10_cout;

  and and_1 (A___B[0], A[0], B[0]);
  and and_2 (and_2_out, A[0], B[1]);
  and and_3 (and_3_out, A[0], B[2]);
  and and_4 (and_4_out, A[0], B[3]);
  and and_5 (and_5_out, A[1], B[0]);
  and and_6 (and_6_out, A[1], B[1]);
  and and_7 (and_7_out, A[1], B[2]);
  and and_8 (and_8_out, A[1], B[3]);
  and and_9 (and_9_out, A[2], B[0]);
  and and_10 (and_10_out, A[2], B[1]);
  and and_11 (and_11_out, A[2], B[2]);
  and and_12 (and_12_out, A[2], B[3]);
  and and_13 (and_13_out, A[3], B[0]);
  and and_14 (and_14_out, A[3], B[1]);
  and and_15 (and_15_out, A[3], B[2]);
  and and_16 (and_16_out, A[3], B[3]);
  Full_Adder _1_Bit_Adder (.A(and_2_out), .B(and_5_out), .Cin(1'b0), .Sum(A___B[1]), .Cout(_1_Bit_Adder_cout));
  Full_Adder full_adder_1 (
    .A(and_3_out), .B(and_6_out), .Cin(_1_Bit_Adder_cout), .Sum(full_adder_1_sum), .Cout(full_adder_1_cout));
  Full_Adder full_adder_2 (
    .A(and_4_out), .B(and_7_out), .Cin(full_adder_1_cout), .Sum(full_adder_2_sum), .Cout(full_adder_2_cout));
  Full_Adder full_adder_3 (
    .A(1'b0), .B(and_8_out), .Cin(full_adder_2_cout), .Sum(full_adder_3_sum), .Cout(full_adder_3_cout));
  Full_Adder full_adder_4 (.A(full_adder_1_sum), .B(and_9_out), .Cin(1'b0), .Sum(A___B[2]), .Cout(full_adder_4_cout));
  Full_Adder full_adder_5 (
    .A(full_adder_2_sum), .B(and_10_out), .Cin(full_adder_4_cout), .Sum(full_adder_5_sum),
    .Cout(full_adder_5_cout));
  Full_Adder full_adder_6 (
    .A(full_adder_3_sum), .B(and_11_out), .Cin(full_adder_5_cout), .Sum(full_adder_6_sum),
    .Cout(full_adder_6_cout));
  Full_Adder full_adder_7 (
    .A(full_adder_3_cout), .B(and_12_out), .Cin(full_adder_6_cout), .Sum(full_adder_7_sum),
    .Cout(full_adder_7_cout));
  Full_Adder full_adder_8 (.A(and_13_out), .B(full_adder_5_sum), .Cin(1'b0), .Sum(A___B[3]), .Cout(full_adder_8_cout));
  Full_Adder full_adder_9 (
    .A(and_14_out), .B(full_adder_6_sum), .Cin(full_adder_8_cout), .Sum(A___B[4]), .Cout(full_adder_9_cout));
  Full_Adder full_adder_10 (
    .A(and_15_out), .B(full_adder_7_sum), .Cin(full_adder_9_cout), .Sum(A___B[5]), .Cout(full_adder_10_cout));
  Full_Adder full_adder_11 (
    .A(and_16_out), .B(full_adder_7_cout), .Cin(full_adder_10_cout), .Sum(A___B[6]), .Cout(A___B[7]));
endmodule
