// Logisim project ALU_2.circ as structural Verilog: 2 circuits, main circuit Multiplier
module Multiplier (
  input  in_1,
  input  [3:0] A,
  input  [3:0] B,
  input  in_4,
  input  in_5,
  input  in_6,
  output [7:0] out_7
);

  wire adder_1_cout, adder_2_cout, adder_2_out, adder_3_cout, adder_3_out, adder_4_cout, adder_4_out,
       adder_5_cout, adder_6_cout, adder_6_out, adder_7_cout, adder_7_out, adder_8_cout, adder_8_out,
       adder_9_cout, adder_10_cout, adder_11_cout, and_2_out, and_3_out, and_4_out, and_5_out, and_6_out,
       and_7_out, and_8_out, and_9_out, and_10_out, and_11_out, and_12_out, and_13_out, and_14_out,
       and_15_out, and_16_out;

  and and_1 (out_7[0], A[0], B[0]);
  and and_2 (and_2_out, A[0], B[1]);
  and and_3 (and_3_out, A[0], B[2]);
  and and_4 (and_4_out, A[0], B[3]);
  and and_5 (and_5_out, A[1], B[0]);
  and and_6 (and_6_out, A[1], B[1]);
  and and_7 (and_7_out, A[1], B[2]);
  and and_8 (and_8_out, A[1], B[3]);
  and and_9 (and_9_out, A[2], B[0]);
  and and_10 (and_10_out, A[2], B[1]);
  and and_11 (and_11_out, A[2], B[2]);
  and and_12 (and_12_out, A[2], B[3]);
  and and_13 (and_13_out, A[3], B[0]);
  and and_14 (and_14_out, A[3], B[1]);
  and and_15 (and_15_out, A[3], B[2]);
  and and_16 (and_16_out, A[3], B[3]);
  Adder #(.width(1)) adder_1 (.a(and_2_out), .b(and_5_out), .out(out_7[1]), .cin(in_1), .cout(adder_1_cout));
  Adder #(.width(1)) adder_2 (.a(and_3_out), .b(and_6_out), .out(adder_2_out), .cin(adder_1_cout), .cout(adder_2_cout));
  Adder #(.width(1)) adder_3 (.a(and_4_out), .b(and_7_out), .out(adder_3_out), .cin(adder_2_cout), .cout(adder_3_cout));
  Adder #(.width(1)) adder_4 (.a(in_4), .b(and_8_out), .out(adder_4_out), .cin(adder_3_cout), .cout(adder_4_cout));
  Adder #(.width(1)) adder_5 (.a(adder_2_out), .b(and_9_out), .out(out_7[2]), .cin(in_5), .cout(adder_5_cout));
  Adder #(.width(1)) adder_6 (
    .a(adder_3_out), .b(and_10_out), .out(adder_6_out), .cin(adder_5_cout), .cout(adder_6_cout));
  Adder #(.width(1)) adder_7 (
    .a(adder_4_out), .b(and_11_out), .out(adder_7_out), .cin(adder_6_cout), .cout(adder_7_cout));
  Adder #(.width(1)) adder_8 (
    .a(adder_4_cout), .b(and_12_out), .out(adder_8_out), .cin(adder_7_cout), .cout(adder_8_cout));
  Adder #(.width(1)) adder_9 (.a(and_13_out), .b(in_6), .out(out_7[3]), .cout(adder_9_cout));  // open: cin
  Adder #(.width(1)) adder_10 (
    .a(and_14_out), .b(adder_7_out), .out(out_7[4]), .cin(adder_9_cout), .cout(adder_10_cout));
  Adder #(.width(1)) adder_11 (
    .a(and_15_out), .b(adder_8_out), .out(out_7[5]), .cin(adder_10_cout), .cout(adder_11_cout));
  Adder #(.width(1)) adder_12 (.a(and_16_out), .b(adder_8_cout), .out(out_7[6]), .cin(adder_11_cout), .cout(out_7[7]));
endmodule

module Adder___Subtractor (
  input  in_1,
  input  in_2,
  input  [3:0] A,
  input  [3:0] A_2,
  input  [3:0] B,
  input  [3:0] B_2,
  input  in_7,
  input  in_8,
  output [3:0] A_B,
  output [3:0] A_B_2
);

  wire adder_1_cout, adder_2_cout, adder_3_cout, subtractor_1_bout, subtractor_2_bout, subtractor_3_bout;

  Adder #(.width(1)) adder_1 (.a(A[0]), .b(B[0]), .out(A_B[0]), .cin(in_1), .cout(adder_1_cout));
  Adder #(.width(1)) adder_2 (.a(A[1]), .b(B[1]), .out(A_B[1]), .cin(adder_1_cout), .cout(adder_2_cout));
  Adder #(.width(1)) adder_3 (.a(A[2]), .b(B[2]), .out(A_B[2]), .cin(adder_2_cout), .cout(adder_3_cout));
  Adder #(.width(1)) adder_4 (.a(A[3]), .b(B[3]), .out(A_B[3]), .cin(adder_3_cout), .cout(in_7));
  Subtractor #(.width(1)) subtractor_1 (.a(A_2[0]), .b(B_2[0]), .out(A_B_2[0]), .bin(in_2), .bout(subtractor_1_bout));
  Subtractor #(.width(1)) subtractor_2 (
    .a(A_2[1]), .b(B_2[1]), .out(A_B_2[1]), .bin(subtractor_1_bout), .bout(subtractor_2_bout));
  Subtractor #(.width(1)) subtractor_3 (
    .a(A_2[2]), .b(B_2[2]), .out(A_B_2[2]), .bin(subtractor_2_bout), .bout(subtractor_3_bout));
  Subtractor #(.width(1)) subtractor_4 (.a(A_2[3]), .b(B_2[3]), .out(A_B_2[3]), .bin(subtractor_3_bout), .bout(in_8));
endmodule
