// Logisim project ALU_Project.circ as structural Verilog: 6 circuits, main circuit ALU
module _2_s_complement (
  input  A0,
  input  A1,
  input  A2,
  input  A3,
  output B0,
  output B1,
  output B2,
  output B3
);

  wire and_1_out, and_2_out, and_3_out, and_4_out, and_5_out, and_6_out, and_7_out, and_8_out, and_9_out,
       and_10_out, and_11_out, and_12_out, not_1_out, not_2_out, not_3_out, not_4_out, not_5_out, not_6_out,
       not_7_out, not_8_out, not_9_out, not_10_out, not_11_out, not_12_out, or_1_out, or_3_out, or_4_out;

  not not_1 (not_1_out, A0);
  not not_2 (not_2_out, A0);
  not not_3 (not_3_out, A0);
  and and_1 (and_1_out, A0, not_4_out);
  not not_4 (not_4_out, A1);
  not not_5 (not_5_out, A2);
  and and_2 (and_2_out, not_5_out, not_6_out);
  not not_6 (not_6_out, A3);
  not not_7 (not_7_out, A1);
  and and_3 (and_3_out, not_7_out, A3);
  not not_8 (not_8_out, A1);
  and and_4 (and_4_out, not_8_out, A2);
  and and_5 (and_5_out, A1, not_9_out);
  not not_9 (not_9_out, A2);
  not not_10 (not_10_out, A3);
  not not_11 (not_11_out, A2);
  and and_6 (and_6_out, not_11_out, A3);
  and and_7 (and_7_out, A2, not_12_out);
  not not_12 (not_12_out, A3);
  and and_8 (and_8_out, not_1_out, A3);
  and and_9 (and_9_out, not_2_out, A2);
  and and_10 (and_10_out, not_3_out, A1);
  and and_11 (and_11_out, and_1_out, and_2_out);
  or or_1 (or_1_out, and_3_out, and_4_out);
  and and_12 (and_12_out, and_5_out, not_10_out);
  or or_2 (B2, and_6_out, and_7_out);
  or or_3 (or_3_out, and_8_out, and_9_out);
  or or_4 (or_4_out, and_10_out, and_11_out);
  or or_5 (B1, or_1_out, and_12_out);
  or or_6 (B0, or_3_out, or_4_out);

  assign B3 = A3;
endmodule

module _1_s_Complement (
  input  A0,
  input  A1,
  input  A2,
  input  A3,
  output B0,
  output B1,
  output B2,
  output B3
);

  not not_1 (B0, A0);
  not not_2 (B1, A1);
  not not_3 (B2, A2);
  not not_4 (B3, A3);
endmodule

module ALU_mux (
  input  S2,
  input  S1,
  input  E2,
  input  E1,
  input  Cin,
  input  A0,
  input  A0_2,
  input  A1,
  input  A1_2,
  input  A2,
  input  A2_2,
  input  B0,
  input  B0_2,
  input  B1,
  input  B1_2,
  input  B2,
  input  B2_2,
  output C0,
  output C0_2,
  output C1,
  output C1_2,
  output C3,
  output C2,
  output C2_2,
  output Co
);

  wire and_1_out, and_2_out, and_3_out, full_adder_1_cout, full_adder_2_cout, full_adder_3_cout, mux_1_out_5,
       mux_2_out_5, mux_3_out_5, not_1_out, not_2_out, not_3_out, or_1_out, or_2_out, or_3_out;

  Full_Adder full_adder_1 (.A(A0), .B(mux_1_out_5), .Cin(Cin), .Sum(C0_2), .Cout(full_adder_1_cout));
  Mux mux_1 (.In_1(B0_2), .S(S1), .In_2(not_1_out), .out_5(mux_1_out_5), .Enable(E1));
  not not_1 (not_1_out, B0_2);
  Full_Adder full_adder_2 (.A(A1), .B(mux_2_out_5), .Cin(full_adder_1_cout), .Sum(C1_2), .Cout(full_adder_2_cout));
  Mux mux_2 (.In_1(B1_2), .S(S1), .In_2(not_2_out), .out_5(mux_2_out_5), .Enable(E1));
  not not_2 (not_2_out, B1_2);
  Full_Adder full_adder_3 (.A(A2), .B(mux_3_out_5), .Cin(full_adder_2_cout), .Sum(C2_2), .Cout(full_adder_3_cout));
  Mux mux_3 (.In_1(B2_2), .S(S1), .In_2(not_3_out), .out_5(mux_3_out_5), .Enable(E1));
  Full_Adder full_adder_4 (.A(1'b0), .B(1'b0), .Cin(full_adder_3_cout), .Sum(C3), .Cout(Co));
  not not_3 (not_3_out, B2_2);
  and and_1 (and_1_out, B2, A2_2);
  Mux mux_4 (.In_1(or_1_out), .S(S2), .In_2(and_1_out), .out_5(C2), .Enable(E2));
  or or_1 (or_1_out, A2_2, B2);
  and and_2 (and_2_out, B1, A1_2);
  Mux mux_5 (.In_1(or_2_out), .S(S2), .In_2(and_2_out), .out_5(C1), .Enable(E2));
  or or_2 (or_2_out, A1_2, B1);
  Mux mux_6 (.In_1(or_3_out), .S(S2), .In_2(and_3_out), .out_5(C0), .Enable(E2));
  or or_3 (or_3_out, B0, A0_2);
  and and_3 (and_3_out, A0_2, B0);

  // Notes on the sheet:
  //   E1 = 0 & E2 = 1
  //   Increment
  //   Addition
  //   Subtraction
  //   1's  Complement
  //   2's Complement
  //   E1 = 1 & E2 = 0
  //   A OR B 
  //   A AND B
  //   FA
  //   Mux
  //   S1 = 0 & Cin = 1
  //   S1 = 0 & Cin = 0 
  //   S1 = 1 & Cin = 1
  //   S1 = 1& Cin=0
  //   S1 =1 & Cin = 1
  //   S2 = 0
  //   S2 = 1
  //   A+B
  //   A-B
  //   B & A is 0
  //   B & A is 0
  //    A or B (NOT BOTH)
endmodule

module BCD_to_7_segment (
  input  D,
  input  C,
  input  B,
  input  A,
  output a_2,
  output b_2,
  output c_2,
  output d_2,
  output e,
  output f,
  output g
);

  wire and_1_out, and_2_out, and_3_out, and_4_out, and_5_out, and_6_out, and_7_out, and_8_out, and_9_out,
       and_10_out, and_11_out, and_12_out, and_13_out, and_14_out, and_15_out, and_16_out, and_17_out,
       and_18_out, not_1_out, not_2_out, not_3_out, not_4_out, not_5_out, not_6_out, not_7_out, not_8_out,
       not_9_out, not_10_out, not_11_out, not_12_out, not_13_out, not_14_out, not_15_out, not_16_out,
       not_17_out, not_18_out, not_19_out, not_20_out, not_21_out, not_22_out, or_1_out, or_2_out, or_3_out,
       or_4_out, or_7_out, or_8_out, or_9_out, or_10_out, or_13_out, or_14_out;

  not not_1 (not_1_out, C);
  and and_1 (and_1_out, not_1_out, not_2_out);
  not not_2 (not_2_out, A);
  not not_3 (not_3_out, C);
  and and_2 (and_2_out, not_3_out, B);
  and and_3 (and_3_out, C, A);
  not not_4 (not_4_out, C);
  not not_5 (not_5_out, B);
  and and_4 (and_4_out, not_5_out, not_6_out);
  not not_6 (not_6_out, A);
  not not_7 (not_7_out, B);
  or or_1 (or_1_out, not_7_out, A);
  not not_8 (not_8_out, C);
  not not_9 (not_9_out, A);
  not not_10 (not_10_out, C);
  not not_11 (not_11_out, A);
  and and_5 (and_5_out, C, not_12_out);
  not not_12 (not_12_out, B);
  not not_13 (not_13_out, C);
  and and_6 (and_6_out, not_13_out, not_14_out);
  not not_14 (not_14_out, A);
  and and_7 (and_7_out, B, not_15_out);
  not not_15 (not_15_out, A);
  not not_16 (not_16_out, B);
  and and_8 (and_8_out, not_16_out, not_17_out);
  not not_17 (not_17_out, A);
  and and_9 (and_9_out, C, not_18_out);
  not not_18 (not_18_out, B);
  and and_10 (and_10_out, C, not_19_out);
  not not_19 (not_19_out, A);
  not not_20 (not_20_out, C);
  and and_11 (and_11_out, not_20_out, B);
  and and_12 (and_12_out, C, not_21_out);
  not not_21 (not_21_out, B);
  and and_13 (and_13_out, C, not_22_out);
  not not_22 (not_22_out, A);
  or or_2 (or_2_out, and_1_out, and_2_out);
  or or_3 (or_3_out, and_3_out, D);
  or or_4 (or_4_out, not_4_out, and_4_out);
  and and_14 (and_14_out, B, A);
  or or_5 (c_2, or_1_out, C);
  and and_15 (and_15_out, not_8_out, not_9_out);
  and and_16 (and_16_out, not_10_out, B);
  and and_17 (and_17_out, B, not_11_out);
  and and_18 (and_18_out, and_5_out, A);
  or or_6 (e, and_6_out, and_7_out);
  or or_7 (or_7_out, and_8_out, and_9_out);
  or or_8 (or_8_out, and_10_out, D);
  or or_9 (or_9_out, and_11_out, and_12_out);
  or or_10 (or_10_out, and_13_out, D);
  or or_11 (a_2, or_2_out, or_3_out);
  or or_12 (b_2, or_4_out, and_14_out);
  or or_13 (or_13_out, and_15_out, and_16_out);
  or or_14 (or_14_out, and_17_out, and_18_out);
  or or_15 (f, or_7_out, or_8_out);
  or or_16 (g, or_9_out, or_10_out);
  or or_17 (d_2, or_13_out, or_14_out);
endmodule

module ALU (
  input  A2,
  input  A1,
  input  A0,
  input  A0_2,
  input  A1_2,
  input  A2_2,
  input  Cin,
  input  S1,
  input  S2,
  input  E2,
  input  E1,
  input  B2,
  input  B1,
  input  B0,
  input  B0_2,
  input  B1_2,
  input  B2_2
);

  wire alu_mux_1_p10, alu_mux_1_p11, alu_mux_1_p12, alu_mux_1_p13, alu_mux_1_p23, alu_mux_1_p24,
       alu_mux_1_p25, and_1_out, bcd_to_7_segment_1_a_2, bcd_to_7_segment_1_b_2, bcd_to_7_segment_1_c_2,
       bcd_to_7_segment_1_d_2, bcd_to_7_segment_1_e, bcd_to_7_segment_1_f, bcd_to_7_segment_1_g, not_1_out,
       or_1_out, or_2_out, or_3_out;

  // ALU_mux alu_mux_1: pin names not known; wires that end beside it: S1, A0, A1, A2, 1'b0, Cin, B0, B1, B2, alu_mux_1_p10, alu_mux_1_p11, alu_mux_1_p12, alu_mux_1_p13, E1, S2, A0_2, A1_2, A2_2, 1'b0, B0_2, B1_2, B2_2, alu_mux_1_p23, alu_mux_1_p24, alu_mux_1_p25, E2
  not not_1 (not_1_out, S1);
  and and_1 (and_1_out, not_1_out, alu_mux_1_p13);
  or or_1 (or_1_out, alu_mux_1_p12, alu_mux_1_p25);
  or or_2 (or_2_out, alu_mux_1_p11, alu_mux_1_p24);
  or or_3 (or_3_out, alu_mux_1_p23, alu_mux_1_p10);
  BCD_to_7_segment bcd_to_7_segment_1 (
    .D(and_1_out), .C(or_1_out), .B(or_2_out), .A(or_3_out), .a_2(bcd_to_7_segment_1_a_2),
    .b_2(bcd_to_7_segment_1_b_2), .c_2(bcd_to_7_segment_1_c_2), .d_2(bcd_to_7_segment_1_d_2),
    .e(bcd_to_7_segment_1_e), .f(bcd_to_7_segment_1_f), .g(bcd_to_7_segment_1_g));
  _7_Segment_Display u_7_segment_display_1 (
    .g(bcd_to_7_segment_1_g), .f(bcd_to_7_segment_1_f), .a(bcd_to_7_segment_1_a_2),
    .b(bcd_to_7_segment_1_b_2), .e(bcd_to_7_segment_1_e), .d(bcd_to_7_segment_1_d_2),
    .c(bcd_to_7_segment_1_c_2));  // open: dp

  // Notes on the sheet:
  //   Decoder
endmodule

module Mux (
  input  In_1,
  input  S,
  input  Enable,
  input  In_2,
  output out_5
);

  wire and_1_out, and_2_out, and_3_out, not_1_out, not_2_out;

  not not_1 (not_1_out, Enable);
  and and_1 (and_1_out, not_1_out, 1'b1);
  not not_2 (not_2_out, S);
  and and_2 (and_2_out, In_1, and_1_out, not_2_out);
  and and_3 (and_3_out, S, and_1_out, In_2);
  or or_1 (out_5, and_2_out, and_3_out);
endmodule
