// Logisim project BCD.circ as structural Verilog
module BCD_to_7_segment (
  input  D,
  input  C,
  input  B,
  input  A,
  output a_2,
  output b_2,
  output c_2,
  output d_2,
  output e,
  output f,
  output g
);

  wire and_1_out, and_2_out, and_3_out, and_4_out, and_5_out, and_6_out, and_7_out, and_8_out, and_9_out,
       and_10_out, and_11_out, and_12_out, and_13_out, and_14_out, and_15_out, and_16_out, and_17_out,
       and_18_out, not_1_out, not_2_out, not_3_out, not_4_out, not_5_out, not_6_out, not_7_out, not_8_out,
       not_9_out, not_10_out, not_11_out, not_12_out, not_13_out, not_14_out, not_15_out, not_16_out,
       not_17_out, not_18_out, not_19_out, not_20_out, not_21_out, not_22_out, or_1_out, or_2_out, or_3_out,
       or_4_out, or_7_out, or_8_out, or_9_out, or_10_out, or_13_out, or_14_out;

  not not_1 (not_1_out, C);
  and and_1 (and_1_out, not_1_out, not_2_out);
  not not_2 (not_2_out, A);
  not not_3 (not_3_out, C);
  and and_2 (and_2_out, not_3_out, B);
  and and_3 (and_3_out, C, A);
  not not_4 (not_4_out, C);
  not not_5 (not_5_out, B);
  and and_4 (and_4_out, not_5_out, not_6_out);
  not not_6 (not_6_out, A);
  not not_7 (not_7_out, B);
  or or_1 (or_1_out, not_7_out, A);
  not not_8 (not_8_out, C);
  not not_9 (not_9_out, A);
  not not_10 (not_10_out, C);
  not not_11 (not_11_out, A);
  and and_5 (and_5_out, C, not_12_out);
  not not_12 (not_12_out, B);
  not not_13 (not_13_out, C);
  and and_6 (and_6_out, not_13_out, not_14_out);
  not not_14 (not_14_out, A);
  and and_7 (and_7_out, B, not_15_out);
  not not_15 (not_15_out, A);
  not not_16 (not_16_out, B);
  and and_8 (and_8_out, not_16_out, not_17_out);
  not not_17 (not_17_out, A);
  and and_9 (and_9_out, C, not_18_out);
  not not_18 (not_18_out, B);
  and and_10 (and_10_out, C, not_19_out);
  not not_19 (not_19_out, A);
  not not_20 (not_20_out, C);
  and and_11 (and_11_out, not_20_out, B);
  and and_12 (and_12_out, C, not_21_out);
  not not_21 (not_21_out, B);
  and and_13 (and_13_out, C, not_22_out);
  not not_22 (not_22_out, A);
  or or_2 (or_2_out, and_1_out, and_2_out);
  or or_3 (or_3_out, and_3_out, D);
  or or_4 (or_4_out, not_4_out, and_4_out);
  and and_14 (and_14_out, B, A);
  or or_5 (c_2, or_1_out, C);
  and and_15 (and_15_out, not_8_out, not_9_out);
  and and_16 (and_16_out, not_10_out, B);
  and and_17 (and_17_out, B, not_11_out);
  and and_18 (and_18_out, and_5_out, A);
  or or_6 (e, and_6_out, and_7_out);
  or or_7 (or_7_out, and_8_out, and_9_out);
  or or_8 (or_8_out, and_10_out, D);
  or or_9 (or_9_out, and_11_out, and_12_out);
  or or_10 (or_10_out, and_13_out, D);
  or or_11 (a_2, or_2_out, or_3_out);
  or or_12 (b_2, or_4_out, and_14_out);
  or or_13 (or_13_out, and_15_out, and_16_out);
  or or_14 (or_14_out, and_17_out, and_18_out);
  or or_15 (f, or_7_out, or_8_out);
  or or_16 (g, or_9_out, or_10_out);
  or or_17 (d_2, or_13_out, or_14_out);
endmodule
